# Fritzing sketch Untitled Sketch (saved by Fritzing 0.9.3b)
breadboards: 2

parts:
  U1 = NodeMCU V1.0
  Componente1 = LCD1602-I2C
  LED1 = DUO LED RG [package="5 mm [THT]"]
  R1 = Resistor [tolerance=±5% resistance=330 package=THT]
  R2 = Resistor [tolerance=±5% resistance=330 package=THT]
  LED2 = LEDs [package=led10mm]
  R3 = Resistor [tolerance=±5% resistance=330 package=THT]
  Mod1 = KY-018 Photoresistor Module [package="Breakout board"]
  Mod2 = KY-020 Tilt Switch Module [package="Breakout board"]
  Mod3 = KY-004 Key Switch Module [package="Breakout board"]
  Mod4 = KY-015 Temperature & Humidity Sensor Module [package="Breakout board"]
  Part1 = KY-006 Passive Buzzer Module [package="Breakout board"]
  R4 = Resistor [tolerance=±5% resistance=220 package=THT]
  R5 = Resistor [tolerance=±5% resistance=220 package=THT]
  LED3 = smd LED [color="Red (633nm)" package="0603 [SMD]"]

nets:
  N1: U1.D0, Part1.S
  N2: U1.D1, Componente1.SCL
  N3: U1.D2, Componente1.SDA
  N4: U1.D3, Mod3.S
  N5: U1.D4, LED2.C
  VIN: U1.3V3, R3.Pin_0, Mod1.-, Mod2.Vin, Mod4.Vin, R4.Pin_1
  GND: U1.GND, Componente1.GND, LED1.red_anode, Mod1.Vin, Mod3.-, Mod4.-, LED3.cathode
  N6: U1.D5, Mod2.S
  N7: U1.D6, R5.Pin_1
  N8: U1.D7, Mod4.S
  N9: U1.D8, R2.Pin_0
  N10: U1.TX, R1.Pin_0
  VIN_2: U1.Vin, Componente1.VCC
  N11: U1.A0, Mod1.S
  N12: LED1.common_cathode, R2.Pin_1
  N13: LED1.green_anode, R1.Pin_1
  N14: LED2.A, R3.Pin_1
  N15: Part1.-, R4.Pin_0
  N16: R5.Pin_0, LED3.anode

custom parts:
  NodeMCU V1.0: ESP8266 based NodeMCU
  LCD1602-I2C: A standard character display, usually with 2x16 characters. Comes in many colors with LCM1602 IIC attached.
  KY-018 Photoresistor Module: KY-018 Photoresistor module, used to measure light intensity. It can determine the presence or absence of light.
  KY-020 Tilt Switch Module: KY-020 tilt switch sensor module. Closes the circuit when it is tilted to the side as long as it is moved with enough force and degree of inclination to activate the ball switch inside.
  KY-004 Key Switch Module: Arduino Key Switch Module Keyes KY-004 is a push button that will output a high signal when pressed.
  KY-015 Temperature & Humidity Sensor Module: KY-015 temperature and humidity sensor module, provides a low-latency serial interface to measure humidity and temperature.
  KY-006 Passive Buzzer Module: Passive Piezoelectric Buzzer Module Keyes KY-006, it can produce a range of sound tones depending on the input frequency.
