# Fritzing sketch Untitled Sketch (saved by Fritzing 0.9.3b)
breadboards: 1

parts:
  U1 = NodeMCU V1.0
  Mod1 = KY-026 Flame Sensor Module [package="Breakout board"]
  LED1 = LED - 3mm [color="Red (635nm)" package="3 mm [THT]"]
  LED2 = LED - 3mm [color="Red (633nm)" package="3 mm [THT]"]
  R1 = Resistor [tolerance=±5% resistance=220 package=THT]
  R2 = Resistor [tolerance=±5% resistance=220 package=THT]
  Mod2 = KY-032 IR Obstacle Avoidance Sensor Module [package="Breakout board"]
  Mod3 = KY-011 Two Color LED Module [package="Breakout board"]
  Mod4 = KY-010 Photo Interrupter Module [package="Breakout board"]

nets:
  N1: U1.D1, Mod1.D0
  N2: U1.D2, LED1.cathode
  N3: U1.D4, LED2.cathode
  N4: U1.GND, Mod2.EN, Mod4.-
  N5: U1.D5, Mod2.out
  N6: U1.D6, Mod4.S
  N7: U1.D7, R2.Pin_1
  N8: U1.D8, R1.Pin_1
  VIN: U1.Vin, Mod1.G, Mod1.+, Mod2.+, Mod4.Vin
  N9: R1.Pin_0, Mod3.S
  N10: R2.Pin_0, Mod3.Vin

custom parts:
  NodeMCU V1.0: ESP8266 based NodeMCU
  KY-026 Flame Sensor Module: KY-026 Flame Sensor Module reacts in the presence of fire.
  KY-032 IR Obstacle Avoidance Sensor Module: KY-032 Infrared Obstacle Avoidance Sensor. Distance-adjustable, infrared proximity sensor designed for wheeled robots. Also known as AD-032.
  KY-011 Two Color LED Module: KY-011 Two Color LED Module consist of a common cathode 3mm red/green LED.
  KY-010 Photo Interrupter Module: KY-010 Photo Interrupter Module, it will trigger a signal when light between the sensor's gap is blocked.
