# Fritzing sketch Untitled Sketch (saved by Fritzing 0.9.3b)
breadboards: 1

parts:
  U1 = NodeMCU V1.0
  Mod1 = KY-004 Key Switch Module [package="Breakout board"]
  R1 = Resistor [tolerance=±5% resistance=220 package="0402 [SMD]"]
  LED1 = LED - 5mm [color="Red (633nm)" package="5 mm [THT]"]
  R2 = Rotary Potentiometer (Large) [maximum_resistance=100kΩ package=THT]
  Mod2 = KY-015 Temperature & Humidity Sensor Module [package="Breakout board"]
  Componente1 = LCD1602-I2C

nets:
  N1: U1.D1, Componente1.SCL
  N2: U1.D2, Componente1.SDA
  N3: U1.D3, Mod1.S
  N4: U1.D4, Mod2.S
  3V3: U1.3V3, Mod2.Vin
  GND: U1.GND, R1.Pin_0, R2.leg1, R2.leg2, Componente1.GND
  N5: U1.D5, LED1.anode
  VIN: U1.Vin, Componente1.VCC
  N6: U1.A0, R2.wiper
  N7: R1.Pin_1, LED1.cathode

custom parts:
  NodeMCU V1.0: ESP8266 based NodeMCU
  KY-004 Key Switch Module: Arduino Key Switch Module Keyes KY-004 is a push button that will output a high signal when pressed.
  KY-015 Temperature & Humidity Sensor Module: KY-015 temperature and humidity sensor module, provides a low-latency serial interface to measure humidity and temperature.
  LCD1602-I2C: A standard character display, usually with 2x16 characters. Comes in many colors with LCM1602 IIC attached.
